// Logisim project main.circ as structural Verilog: 5 circuits, main circuit main
module main (
  input  [7:0] in_1,
  input  in_2,
  output [7:0] out_3
);

  wire clock_1_out;

  Clock clock_1 (.out(clock_1_out));
  _8_Bit_Register u_8_bit_register_1 (.Q(out_3), .C(clock_1_out), .E(in_2), .D(in_1));
endmodule

module D_Latch (
  input  D,
  input  E,
  output Q
);

  wire nand_1_out, nand_2_out, nand_4_out;

  nand nand_1 (nand_1_out, D, E);
  nand nand_2 (nand_2_out, nand_1_out, E);
  nand nand_3 (Q, nand_1_out, nand_4_out);
  nand nand_4 (nand_4_out, Q, nand_2_out);
endmodule

module _8_Bit_Memory (
  input  [7:0] I,
  input  E,
  output [7:0] O
);

  D_Latch d_latch_1 (.Q(O[0]), .E(E), .D(I[0]));
  D_Latch d_latch_2 (.Q(O[1]), .E(E), .D(I[1]));
  D_Latch d_latch_3 (.Q(O[2]), .E(E), .D(I[2]));
  D_Latch d_latch_4 (.Q(O[3]), .E(E), .D(I[3]));
  D_Latch d_latch_5 (.Q(O[4]), .E(E), .D(I[4]));
  D_Latch d_latch_6 (.Q(O[5]), .E(E), .D(I[5]));
  D_Latch d_latch_7 (.Q(O[6]), .E(E), .D(I[6]));
  D_Latch d_latch_8 (.Q(O[7]), .E(E), .D(I[7]));
endmodule

module _8_Bit_Enabler (
  input  [7:0] D,
  input  E,
  output [7:0] Q
);

  and and_1 (Q[0], D[0], E);
  and and_2 (Q[1], D[1], E);
  and and_3 (Q[2], D[2], E);
  and and_4 (Q[3], D[3], E);
  and and_5 (Q[4], D[4], E);
  and and_6 (Q[5], D[5], E);
  and and_7 (Q[6], D[6], E);
  and and_8 (Q[7], D[7], E);
endmodule

module _8_Bit_Register (
  input  [7:0] D,
  input  C,
  input  E,
  output [7:0] Q
);

  wire [7:0] n8_bit_memory_1_o;

  _8_Bit_Memory u_8_bit_memory_1 (.O(n8_bit_memory_1_o), .I(D), .E(C));
  _8_Bit_Enabler u_8_bit_enabler_1 (.Q(Q), .D(n8_bit_memory_1_o), .E(E));
endmodule
